// Digital circuit alu.dig as structural Verilog
module alu (
  input  [31:0] A,
  input  [31:0] B,
  input  [3:0] ALUOp,
  output [31:0] Result,
  output FlagZ
);

  wire add_sub_unit_1_overflow, add_sub_unit_1_sign, and_1_out, and_2_out, not_1_out, or_1_out, or_2_out;
  wire [0:0] slt_unit_1_out, xor_1_out;
  wire [31:0] add_sub_unit_1_out, bidirectional_shifter_1_out, boolean_unit_1_out, multiplexer_1_out,
       multiplexer_2_out;

  xor xor_1 (xor_1_out[0], ALUOp[0], ALUOp[1]);
  and and_1 (and_1_out, ALUOp[1], ALUOp[2]);
  add_sub_unit add_sub_unit_1 (
    .A(A), .B(B), .Sub(and_1_out), .Out(add_sub_unit_1_out), .Sign(add_sub_unit_1_sign),
    .Overflow(add_sub_unit_1_overflow));
  boolean_unit boolean_unit_1 (.A(A), .B(B), .Bool({ALUOp[1], xor_1_out[0]}), .Out(boolean_unit_1_out));
  bidirectional_shifter bidirectional_shifter_1 (
    .A(A), .B(B), .ShiftOp({ALUOp[3], ALUOp[0]}), .Out(bidirectional_shifter_1_out));
  slt_unit slt_unit_1 (.Sign(add_sub_unit_1_sign), .Overflow(add_sub_unit_1_overflow), .Out(slt_unit_1_out[0]));
  Multiplexer #(.Bits(32)) multiplexer_1 (
    .sel(or_1_out), .in_0(boolean_unit_1_out), .in_1(bidirectional_shifter_1_out), .out(multiplexer_1_out));
  or or_1 (or_1_out, ALUOp[2], ALUOp[3]);
  Multiplexer #(.Bits(32)) multiplexer_2 (
    .sel(ALUOp[0]), .in_0(add_sub_unit_1_out), .in_1({{31{1'b0}}, slt_unit_1_out[0]}), .out(multiplexer_2_out));
  Multiplexer #(.Bits(32)) multiplexer_3 (
    .sel(and_2_out), .in_0(multiplexer_1_out), .in_1(multiplexer_2_out), .out(Result));
  and and_2 (and_2_out, or_2_out, ALUOp[1]);
  or or_2 (or_2_out, ALUOp[2], not_1_out);
  not not_1 (not_1_out, ALUOp[0]);
  Comparator #(.Bits(32)) comparator_1 (.a(Result), .b({32{1'b0}}), .eq(FlagZ));  // open: gt, lt

  // Other names for the same wires on the sheet: a_0 = ALUOp[0]; a_1 = ALUOp[1]; a_2 = ALUOp[2]; a_3 = ALUOp[3]
endmodule

/* Test case alu tests:
A B ALUOp Result FlagZ
0x00000000 0x00000000 0 0x00000000 1
0x00000000 0x00000000 1 0x00000000 1
0x00000000 0x00000000 2 0x00000000 1
0x00000000 0x00000000 3 0x00000000 1
0x00000000 0x00000000 4 0x00000000 1
0x00000000 0x00000000 5 0x00000000 1
0x00000000 0x00000000 6 0x00000000 1
0x00000000 0x00000000 7 0x00000000 1
0x00000000 0x00000000 8 0x00000000 1
0x00000000 0x00000001 0 0x00000000 1
0x00000000 0x00000001 1 0x00000001 0
0x00000000 0x00000001 2 0x00000001 0
0x00000000 0x00000001 3 0x00000001 0
0x00000000 0x00000001 4 0x00000000 1
0x00000000 0x00000001 5 0x00000000 1
0x00000000 0x00000001 6 0xFFFFFFFF 0
0x00000000 0x00000001 7 0x00000001 0
0x00000000 0x00000001 8 0x00000000 1
0x00000001 0x00000000 0 0x00000000 1
0x00000001 0x00000000 1 0x00000001 0
0x00000001 0x00000000 2 0x00000001 0
0x00000001 0x00000000 3 0x00000001 0
0x00000001 0x00000000 4 0x00000001 0
0x00000001 0x00000000 5 0x00000001 0
0x00000001 0x00000000 6 0x00000001 0
0x00000001 0x00000000 7 0x00000000 1
0x00000001 0x00000000 8 0x00000001 0
0x00000001 0x00000001 0 0x00000001 0
0x00000001 0x00000001 1 0x00000001 0
0x00000001 0x00000001 2 0x00000002 0
0x00000001 0x00000001 3 0x00000000 1
0x00000001 0x00000001 4 0x00000002 0
0x00000001 0x00000001 5 0x00000000 1
0x00000001 0x00000001 6 0x00000000 1
0x00000001 0x00000001 7 0x00000000 1
0x00000001 0x00000001 8 0x00000000 1
0x00000004 0x00000005 0 0x00000004 0
0x00000004 0x00000005 1 0x00000005 0
0x00000004 0x00000005 2 0x00000009 0
0x00000004 0x00000005 3 0x00000001 0
0x00000004 0x00000005 4 0x00000080 0
0x00000004 0x00000005 5 0x00000000 1
0x00000004 0x00000005 6 0xFFFFFFFF 0
0x00000004 0x00000005 7 0x00000001 0
0x00000004 0x00000005 8 0x00000000 1
0x00000003 0x00000001 0 0x00000001 0
0x00000003 0x00000001 1 0x00000003 0
0x00000003 0x00000001 2 0x00000004 0
0x00000003 0x00000001 3 0x00000002 0
0x00000003 0x00000001 4 0x00000006 0
0x00000003 0x00000001 5 0x00000001 0
0x00000003 0x00000001 6 0x00000002 0
0x00000003 0x00000001 7 0x00000000 1
0x00000003 0x00000001 8 0x00000001 0
0xFFFFFFFF 0x00000001 0 0x00000001 0
0xFFFFFFFF 0x00000001 1 0xFFFFFFFF 0
0xFFFFFFFF 0x00000001 2 0x00000000 1
0xFFFFFFFF 0x00000001 3 0xFFFFFFFE 0
0xFFFFFFFF 0x00000001 4 0xFFFFFFFE 0
0xFFFFFFFF 0x00000001 5 0x7FFFFFFF 0
0xFFFFFFFF 0x00000001 6 0xFFFFFFFE 0
0xFFFFFFFF 0x00000001 7 0x00000001 0
0xFFFFFFFF 0x00000001 8 0xFFFFFFFF 0
0x7FFFFFFF 0x00000001 0 0x00000001 0
0x7FFFFFFF 0x00000001 1 0x7FFFFFFF 0
0x7FFFFFFF 0x00000001 2 0x80000000 0
0x7FFFFFFF 0x00000001 3 0x7FFFFFFE 0
0x7FFFFFFF 0x00000001 4 0xFFFFFFFE 0
0x7FFFFFFF 0x00000001 5 0x3FFFFFFF 0
0x7FFFFFFF 0x00000001 6 0x7FFFFFFE 0
0x7FFFFFFF 0x00000001 7 0x00000000 1
0x7FFFFFFF 0x00000001 8 0x3FFFFFFF 0
0x80000000 0x00000001 0 0x00000000 1
0x80000000 0x00000001 1 0x80000001 0
0x80000000 0x00000001 2 0x80000001 0
0x80000000 0x00000001 3 0x80000001 0
0x80000000 0x00000001 4 0x00000000 1
0x80000000 0x00000001 5 0x40000000 0
0x80000000 0x00000001 6 0x7FFFFFFF 0
0x80000000 0x00000001 7 0x00000001 0
0x80000000 0x00000001 8 0xC0000000 0
0x00000000 0x80000000 0 0x00000000 1
0x00000000 0x80000000 1 0x80000000 0
0x00000000 0x80000000 2 0x80000000 0
0x00000000 0x80000000 3 0x80000000 0
0x00000000 0x80000000 4 0x00000000 1
0x00000000 0x80000000 5 0x00000000 1
0x00000000 0x80000000 6 0x80000000 0
0x00000000 0x80000000 7 0x00000000 1
0x00000000 0x80000000 8 0x00000000 1
0x80000000 0xFFFFFFFF 0 0x80000000 0
0x80000000 0xFFFFFFFF 1 0xFFFFFFFF 0
0x80000000 0xFFFFFFFF 2 0x7FFFFFFF 0
0x80000000 0xFFFFFFFF 3 0x7FFFFFFF 0
0x80000000 0xFFFFFFFF 4 0x00000000 1
0x80000000 0xFFFFFFFF 5 0x00000001 0
0x80000000 0xFFFFFFFF 6 0x80000001 0
0x80000000 0xFFFFFFFF 7 0x00000001 0
0x80000000 0xFFFFFFFF 8 0xFFFFFFFF 0
0x7FFFFFFF 0xFFFFFFFF 0 0x7FFFFFFF 0
0x7FFFFFFF 0xFFFFFFFF 1 0xFFFFFFFF 0
0x7FFFFFFF 0xFFFFFFFF 2 0x7FFFFFFE 0
0x7FFFFFFF 0xFFFFFFFF 3 0x80000000 0
0x7FFFFFFF 0xFFFFFFFF 4 0x80000000 0
0x7FFFFFFF 0xFFFFFFFF 5 0x00000000 1
0x7FFFFFFF 0xFFFFFFFF 6 0x80000000 0
0x7FFFFFFF 0xFFFFFFFF 7 0x00000000 1
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*/
