// Digital circuit bidirectional-shifter.dig as structural Verilog
module bidirectional_shifter (
  input  [31:0] A,
  input  [31:0] B,
  input  [1:0] ShiftOp,
  output [31:0] Out
);

  wire [31:0] barrelshifter_1_out, barrelshifter_2_out, barrelshifter_3_out;

  BarrelShifter #(.Bits(32)) barrelshifter_1 (.in(A), .shift({1'b0, B[4:0]}), .out(barrelshifter_1_out));
  BarrelShifter #(.Bits(32), .direction("right")) barrelshifter_2 (
    .in(A), .shift({1'b0, B[4:0]}), .out(barrelshifter_2_out));
  BarrelShifter #(.barrelShifterMode("arithmetic"), .Bits(32), .direction("right")) barrelshifter_3 (
    .in(A), .shift({1'b0, B[4:0]}), .out(barrelshifter_3_out));
  Multiplexer #(.Bits(32), .Selector_Bits(2)) multiplexer_1 (
    .sel(ShiftOp), .in_0(barrelshifter_1_out), .in_1(barrelshifter_2_out), .in_2(barrelshifter_3_out),
    .in_3(barrelshifter_3_out), .out(Out));

  // Other names for the same wires on the sheet: B_t[4:0] = B[4:0]
endmodule

/* Test case bidirectional-shifter tests:
A B ShiftOp Out
0x00000000 0x00000000 0 0x00000000
0x00000000 0x00000000 1 0x00000000
0x00000000 0x00000000 2 0x00000000
0x00000000 0x00000001 0 0x00000000
0x00000000 0x00000001 1 0x00000000
0x00000000 0x00000001 2 0x00000000
0x00000000 0x00000004 0 0x00000000
0x00000000 0x00000004 1 0x00000000
0x00000000 0x00000004 2 0x00000000
0x00000000 0x0000001F 0 0x00000000
0x00000000 0x0000001F 1 0x00000000
0x00000000 0x0000001F 2 0x00000000
0x00000000 0x00000020 0 0x00000000
0x00000000 0x00000020 1 0x00000000
0x00000000 0x00000020 2 0x00000000
0x00000000 0x00000021 0 0x00000000
0x00000000 0x00000021 1 0x00000000
0x00000000 0x00000021 2 0x00000000
0x00000000 0xFFFFFFFF 0 0x00000000
0x00000000 0xFFFFFFFF 1 0x00000000
0x00000000 0xFFFFFFFF 2 0x00000000
0x00000001 0x00000000 0 0x00000001
0x00000001 0x00000000 1 0x00000001
0x00000001 0x00000000 2 0x00000001
0x00000001 0x00000001 0 0x00000002
0x00000001 0x00000001 1 0x00000000
0x00000001 0x00000001 2 0x00000000
0x00000001 0x00000004 0 0x00000010
0x00000001 0x00000004 1 0x00000000
0x00000001 0x00000004 2 0x00000000
0x00000001 0x0000001F 0 0x80000000
0x00000001 0x0000001F 1 0x00000000
0x00000001 0x0000001F 2 0x00000000
0x00000001 0x00000020 0 0x00000001
0x00000001 0x00000020 1 0x00000001
0x00000001 0x00000020 2 0x00000001
0x00000001 0x00000021 0 0x00000002
0x00000001 0x00000021 1 0x00000000
0x00000001 0x00000021 2 0x00000000
0x00000001 0xFFFFFFFF 0 0x80000000
0x00000001 0xFFFFFFFF 1 0x00000000
0x00000001 0xFFFFFFFF 2 0x00000000
0x80000001 0x00000000 0 0x80000001
0x80000001 0x00000000 1 0x80000001
0x80000001 0x00000000 2 0x80000001
0x80000001 0x00000001 0 0x00000002
0x80000001 0x00000001 1 0x40000000
0x80000001 0x00000001 2 0xC0000000
0x80000001 0x00000004 0 0x00000010
0x80000001 0x00000004 1 0x08000000
0x80000001 0x00000004 2 0xF8000000
0x80000001 0x0000001F 0 0x80000000
0x80000001 0x0000001F 1 0x00000001
0x80000001 0x0000001F 2 0xFFFFFFFF
0x80000001 0x00000020 0 0x80000001
0x80000001 0x00000020 1 0x80000001
0x80000001 0x00000020 2 0x80000001
0x80000001 0x00000021 0 0x00000002
0x80000001 0x00000021 1 0x40000000
0x80000001 0x00000021 2 0xC0000000
0x80000001 0xFFFFFFFF 0 0x80000000
0x80000001 0xFFFFFFFF 1 0x00000001
0x80000001 0xFFFFFFFF 2 0xFFFFFFFF
0xFFFFFFFF 0x00000000 0 0xFFFFFFFF
0xFFFFFFFF 0x00000000 1 0xFFFFFFFF
0xFFFFFFFF 0x00000000 2 0xFFFFFFFF
0xFFFFFFFF 0x00000001 0 0xFFFFFFFE
0xFFFFFFFF 0x00000001 1 0x7FFFFFFF
0xFFFFFFFF 0x00000001 2 0xFFFFFFFF
0xFFFFFFFF 0x00000004 0 0xFFFFFFF0
0xFFFFFFFF 0x00000004 1 0x0FFFFFFF
0xFFFFFFFF 0x00000004 2 0xFFFFFFFF
0xFFFFFFFF 0x0000001F 0 0x80000000
0xFFFFFFFF 0x0000001F 1 0x00000001
0xFFFFFFFF 0x0000001F 2 0xFFFFFFFF
0xFFFFFFFF 0x00000020 0 0xFFFFFFFF
0xFFFFFFFF 0x00000020 1 0xFFFFFFFF
0xFFFFFFFF 0x00000020 2 0xFFFFFFFF
0xFFFFFFFF 0x00000021 0 0xFFFFFFFE
0xFFFFFFFF 0x00000021 1 0x7FFFFFFF
0xFFFFFFFF 0x00000021 2 0xFFFFFFFF
0xFFFFFFFF 0xFFFFFFFF 0 0x80000000
0xFFFFFFFF 0xFFFFFFFF 1 0x00000001
0xFFFFFFFF 0xFFFFFFFF 2 0xFFFFFFFF
0x12345678 0x00000000 0 0x12345678
0x12345678 0x00000000 1 0x12345678
0x12345678 0x00000000 2 0x12345678
0x12345678 0x00000001 0 0x2468ACF0
0x12345678 0x00000001 1 0x091A2B3C
0x12345678 0x00000001 2 0x091A2B3C
0x12345678 0x00000004 0 0x23456780
0x12345678 0x00000004 1 0x01234567
0x12345678 0x00000004 2 0x01234567
0x12345678 0x0000001F 0 0x00000000
0x12345678 0x0000001F 1 0x00000000
0x12345678 0x0000001F 2 0x00000000
0x12345678 0x00000020 0 0x12345678
0x12345678 0x00000020 1 0x12345678
0x12345678 0x00000020 2 0x12345678
0x12345678 0x00000021 0 0x2468ACF0
0x12345678 0x00000021 1 0x091A2B3C
0x12345678 0x00000021 2 0x091A2B3C
0x12345678 0xFFFFFFFF 0 0x00000000
0x12345678 0xFFFFFFFF 1 0x00000000
0x12345678 0xFFFFFFFF 2 0x00000000
*/
